# Fritzing sketch pressurePadDiagram (saved by Fritzing 0.9.3b)
breadboards: 1

parts:
  Pressure_Sensor_Circuit = Arduino Uno (Rev3)
  part = Resistor [tolerance=±5% resistance=500 package=THT]
  Force_Sensor = Basic Force Sensing Resistor (FSR) [package=THT]

nets:
  N1: Pressure_Sensor_Circuit.A4/SDA, part.Pin_1
  N2: Pressure_Sensor_Circuit.5V, Force_Sensor.pin_0
  N3: part.Pin_0, Force_Sensor.pin_1
