# Fritzing sketch sensorsCircuit (saved by Fritzing 0.9.3b)
breadboards: 1

parts:
  Bottom_Clock_Arduino_Sensors_Circuit = Arduino Uno (Rev3)
  part = Resistor [tolerance=±5% resistance=500 package=THT]
  Force_Sensor = Basic Force Sensing Resistor (FSR) [package=THT]
  Distance_Sensor_3 = Infrared Proximity Sensor
  Distance_Sensor_2 = Infrared Proximity Sensor
  Distance_Sensor_1 = Infrared Proximity Sensor
  IR1 = PHOTOTRANSISTOR REFLECTIVE OBJECT SENSOR [package=qrb1114-side]
  IR2 = PHOTOTRANSISTOR REFLECTIVE OBJECT SENSOR [package=qrb1114-side]
  IR3 = PHOTOTRANSISTOR REFLECTIVE OBJECT SENSOR [package=qrb1114-side]
  IR4 = PHOTOTRANSISTOR REFLECTIVE OBJECT SENSOR [package=qrb1114-side]
  Sensor_LED_Strip = Luxeon LED [package=luxeon]
  Animal_LED_Strip = Luxeon LED [package=luxeon]
  part_2 = Resistor [tolerance=±5% resistance=365 package=THT]
  part_3 = Resistor [tolerance=±5% resistance=365 package=THT]

nets:
  N1: Bottom_Clock_Arduino_Sensors_Circuit.A0, Distance_Sensor_1.Vout
  N2: Bottom_Clock_Arduino_Sensors_Circuit.A1, Distance_Sensor_2.Vout
  N3: Bottom_Clock_Arduino_Sensors_Circuit.A2, Distance_Sensor_3.Vout
  N4: Bottom_Clock_Arduino_Sensors_Circuit.A4/SDA, part.Pin_1
  N5: Bottom_Clock_Arduino_Sensors_Circuit.D9_PWM, IR1.C
  N6: Bottom_Clock_Arduino_Sensors_Circuit.D10_PWM/SS, IR2.C
  N7: Bottom_Clock_Arduino_Sensors_Circuit.D11_PWM/MOSI, IR3.C
  N8: Bottom_Clock_Arduino_Sensors_Circuit.D12/MISO, IR4.C
  GND: Bottom_Clock_Arduino_Sensors_Circuit.GND, Distance_Sensor_3.GND, Distance_Sensor_2.GND, Distance_Sensor_1.GND, IR1.E, IR1.K, IR2.E, IR2.K, IR3.E, IR3.K, IR4.E, IR4.K, Sensor_LED_Strip.C, Animal_LED_Strip.C
  VCC: Bottom_Clock_Arduino_Sensors_Circuit.5V, Force_Sensor.pin_0, Distance_Sensor_3.Vcc, Distance_Sensor_2.Vcc, Distance_Sensor_1.Vcc, IR1.A, IR2.A, IR3.A, IR4.A, Sensor_LED_Strip.A, Animal_LED_Strip.A
  N9: part.Pin_0, Force_Sensor.pin_1
  N10: Sensor_LED_Strip.S, part_2.Pin_1
  N11: Animal_LED_Strip.S, part_3.Pin_1
